// Digital circuit 16Bit_2 to 1_Mux.dig as structural Verilog
module _16Bit_2_to_1_Mux (
  input  S_0,
  input  A_0,
  input  A_1,
  input  A_2,
  input  A_3,
  input  A_4,
  input  A_5,
  input  A_6,
  input  A_7,
  input  A_8,
  input  A_9,
  input  A_10,
  input  A_11,
  input  A_12,
  input  A_13,
  input  A_14,
  input  A_15,
  input  B_0,
  input  B_1,
  input  B_2,
  input  B_3,
  input  B_4,
  input  B_5,
  input  B_6,
  input  B_7,
  input  B_8,
  input  B_9,
  input  B_10,
  input  B_11,
  input  B_12,
  input  B_13,
  input  B_14,
  input  B_15,
  output Out_0,
  output Out_1,
  output Out_2,
  output Out_3,
  output Out_4,
  output Out_5,
  output Out_6,
  output Out_7,
  output Out_8,
  output Out_9,
  output Out_10,
  output Out_11,
  output Out_12,
  output Out_13,
  output Out_14,
  output Out_15
);

  _2_to_1_Mux _2_to_1_mux_1 (.I_1(B_0), .I_0(A_0), .S_0(S_0), .Out(Out_0));
  _2_to_1_Mux _2_to_1_mux_2 (.I_1(B_1), .I_0(A_1), .S_0(S_0), .Out(Out_1));
  _2_to_1_Mux _2_to_1_mux_3 (.I_1(B_2), .I_0(A_2), .S_0(S_0), .Out(Out_2));
  _2_to_1_Mux _2_to_1_mux_4 (.I_1(B_3), .I_0(A_3), .S_0(S_0), .Out(Out_3));
  _2_to_1_Mux _2_to_1_mux_5 (.I_1(B_4), .I_0(A_4), .S_0(S_0), .Out(Out_4));
  _2_to_1_Mux _2_to_1_mux_6 (.I_1(B_5), .I_0(A_5), .S_0(S_0), .Out(Out_5));
  _2_to_1_Mux _2_to_1_mux_7 (.I_1(B_6), .I_0(A_6), .S_0(S_0), .Out(Out_6));
  _2_to_1_Mux _2_to_1_mux_8 (.I_1(B_7), .I_0(A_7), .S_0(S_0), .Out(Out_7));
  _2_to_1_Mux _2_to_1_mux_9 (.I_1(B_8), .I_0(A_8), .S_0(S_0), .Out(Out_8));
  _2_to_1_Mux _2_to_1_mux_10 (.I_1(B_9), .I_0(A_9), .S_0(S_0), .Out(Out_9));
  _2_to_1_Mux _2_to_1_mux_11 (.I_1(B_10), .I_0(A_10), .S_0(S_0), .Out(Out_10));
  _2_to_1_Mux _2_to_1_mux_12 (.I_1(B_11), .I_0(A_11), .S_0(S_0), .Out(Out_11));
  _2_to_1_Mux _2_to_1_mux_13 (.I_1(B_12), .I_0(A_12), .S_0(S_0), .Out(Out_12));
  _2_to_1_Mux _2_to_1_mux_14 (.I_1(B_13), .I_0(A_13), .S_0(S_0), .Out(Out_13));
  _2_to_1_Mux _2_to_1_mux_15 (.I_1(B_14), .I_0(A_14), .S_0(S_0), .Out(Out_14));
  _2_to_1_Mux _2_to_1_mux_16 (.I_1(B_15), .I_0(A_15), .S_0(S_0), .Out(Out_15));
endmodule
