// Digital circuit 16Bit_AndArray.dig as structural Verilog
module _16Bit_AndArray (
  input  In_15,
  input  In_14,
  input  In_13,
  input  In_12,
  input  In_11,
  input  In_10,
  input  In_9,
  input  In_8,
  input  In_7,
  input  In_6,
  input  In_5,
  input  In_4,
  input  In_3,
  input  In_2,
  input  In_1,
  input  In_0,
  input  Rd,
  output Out_2,
  output Out_1,
  output Out_0,
  output Out_5,
  output Out_4,
  output Out_3,
  output Out_8,
  output Out_7,
  output Out_6,
  output Out_11,
  output Out_10,
  output Out_9,
  output Out_14,
  output Out_13,
  output Out_12,
  output Out_15
);

  and and_1 (Out_15, In_15, Rd);
  and and_2 (Out_14, In_14, Rd);
  and and_3 (Out_13, In_13, Rd);
  and and_4 (Out_12, In_12, Rd);
  and and_5 (Out_11, In_11, Rd);
  and and_6 (Out_10, In_10, Rd);
  and and_7 (Out_9, In_9, Rd);
  and and_8 (Out_8, In_8, Rd);
  and and_9 (Out_7, In_7, Rd);
  and and_10 (Out_6, In_6, Rd);
  and and_11 (Out_5, In_5, Rd);
  and and_12 (Out_4, In_4, Rd);
  and and_13 (Out_3, In_3, Rd);
  and and_14 (Out_2, In_2, Rd);
  and and_15 (Out_1, In_1, Rd);
  and and_16 (Out_0, In_0, Rd);
endmodule
