// Digital circuit 16bit_Reg.dig as structural Verilog
module _16bit_Reg (
  input  In_1,
  input  Clk,
  input  Wrt,
  input  In_2,
  input  In_3,
  input  In_4,
  input  In_5,
  input  In_6,
  input  In_7,
  input  In_8,
  input  In_9,
  input  In_10,
  input  In_11,
  input  In_12,
  input  In_13,
  input  In_14,
  input  In_15,
  input  In_16,
  input  Rd,
  output Out_1,
  output Out_2,
  output Out_3,
  output Out_4,
  output Out_5,
  output Out_6,
  output Out_7,
  output Out_8,
  output Out_9,
  output Out_10,
  output Out_11,
  output Out_12,
  output Out_13,
  output Out_14,
  output Out_15,
  output Out_16
);

  wire _1bit_regcell_1_out, _1bit_regcell_2_out, _1bit_regcell_3_out, _1bit_regcell_4_out,
       _1bit_regcell_5_out, _1bit_regcell_6_out, _1bit_regcell_7_out, _1bit_regcell_8_out,
       _1bit_regcell_9_out, _1bit_regcell_10_out, _1bit_regcell_11_out, _1bit_regcell_12_out,
       _1bit_regcell_13_out, _1bit_regcell_14_out, _1bit_regcell_15_out, _1bit_regcell_16_out, and_1_out;

  and and_1 (and_1_out, Wrt, Clk);
  _1Bit_RegCell _1bit_regcell_1 (.In(In_1), .Clk(and_1_out), .Out(_1bit_regcell_1_out));
  _1Bit_RegCell _1bit_regcell_2 (.In(In_2), .Clk(and_1_out), .Out(_1bit_regcell_2_out));
  _1Bit_RegCell _1bit_regcell_3 (.In(In_3), .Clk(and_1_out), .Out(_1bit_regcell_3_out));
  _1Bit_RegCell _1bit_regcell_4 (.In(In_4), .Clk(and_1_out), .Out(_1bit_regcell_4_out));
  _1Bit_RegCell _1bit_regcell_5 (.In(In_5), .Clk(and_1_out), .Out(_1bit_regcell_5_out));
  _1Bit_RegCell _1bit_regcell_6 (.In(In_6), .Clk(and_1_out), .Out(_1bit_regcell_6_out));
  _1Bit_RegCell _1bit_regcell_7 (.In(In_7), .Clk(and_1_out), .Out(_1bit_regcell_7_out));
  _1Bit_RegCell _1bit_regcell_8 (.In(In_8), .Clk(and_1_out), .Out(_1bit_regcell_8_out));
  _1Bit_RegCell _1bit_regcell_9 (.In(In_9), .Clk(and_1_out), .Out(_1bit_regcell_9_out));
  _1Bit_RegCell _1bit_regcell_10 (.In(In_10), .Clk(and_1_out), .Out(_1bit_regcell_10_out));
  _1Bit_RegCell _1bit_regcell_11 (.In(In_11), .Clk(and_1_out), .Out(_1bit_regcell_11_out));
  _1Bit_RegCell _1bit_regcell_12 (.In(In_12), .Clk(and_1_out), .Out(_1bit_regcell_12_out));
  _1Bit_RegCell _1bit_regcell_13 (.In(In_13), .Clk(and_1_out), .Out(_1bit_regcell_13_out));
  _1Bit_RegCell _1bit_regcell_14 (.In(In_14), .Clk(and_1_out), .Out(_1bit_regcell_14_out));
  _1Bit_RegCell _1bit_regcell_15 (.In(In_15), .Clk(and_1_out), .Out(_1bit_regcell_15_out));
  _1Bit_RegCell _1bit_regcell_16 (.In(In_16), .Clk(and_1_out), .Out(_1bit_regcell_16_out));
  _16Bit_AndArray _16bit_andarray_1 (
    .Out_15(Out_16), .Out_14(Out_15), .Out_13(Out_14), .Out_12(Out_13), .Out_11(Out_12), .Out_10(Out_11),
    .Out_9(Out_10), .Out_8(Out_9), .Out_7(Out_8), .Out_6(Out_7), .Out_5(Out_6), .Out_4(Out_5), .Out_3(Out_4),
    .Out_2(Out_3), .Out_1(Out_2), .Out_0(Out_1), .In_15(_1bit_regcell_16_out), .In_14(_1bit_regcell_15_out),
    .In_13(_1bit_regcell_14_out), .In_12(_1bit_regcell_13_out), .In_11(_1bit_regcell_12_out),
    .In_10(_1bit_regcell_11_out), .In_9(_1bit_regcell_10_out), .In_8(_1bit_regcell_9_out),
    .In_7(_1bit_regcell_8_out), .In_6(_1bit_regcell_7_out), .In_5(_1bit_regcell_6_out),
    .In_4(_1bit_regcell_5_out), .In_3(_1bit_regcell_4_out), .In_2(_1bit_regcell_3_out),
    .In_1(_1bit_regcell_2_out), .In_0(_1bit_regcell_1_out), .Rd(Rd));
endmodule
