// Digital circuit 1Bit_FullAdder.dig as structural Verilog
module _1Bit_FullAdder (
  input  A,
  input  B,
  input  C_in,
  output S,
  output C_out
);

  wire and_1_out, and_2_out, xor_1_out;

  xor xor_1 (xor_1_out, A, B);
  xor xor_2 (S, xor_1_out, C_in);
  and and_1 (and_1_out, C_in, xor_1_out);
  and and_2 (and_2_out, A, B);
  or or_1 (C_out, and_1_out, and_2_out);
endmodule
