// Digital circuit 1Bit_RegCell.dig as structural Verilog
module _1Bit_RegCell (
  input  In,
  input  Clk,
  output Out
);

  wire nand_1_out, nand_2_out, nand_3_out, nand_4_out, nand_5_out, nand_6_out, nand_7_out, not_1_out,
       not_2_out;

  not not_1 (not_1_out, In);
  nand nand_1 (nand_1_out, Clk, In);
  nand nand_2 (nand_2_out, Clk, not_1_out);
  nand nand_3 (nand_3_out, nand_4_out, nand_1_out);
  nand nand_4 (nand_4_out, nand_2_out, nand_3_out);
  not not_2 (not_2_out, Clk);
  nand nand_5 (nand_5_out, not_2_out, nand_4_out);
  nand nand_6 (nand_6_out, nand_3_out, not_2_out);
  nand nand_7 (nand_7_out, Out, nand_5_out);
  nand nand_8 (Out, nand_6_out, nand_7_out);
endmodule
