// Digital circuit 4 to 1_Mux.dig as structural Verilog
module _4_to_1_Mux (
  input  S_1,
  input  S_0,
  input  I_3,
  input  I_2,
  input  I_1,
  input  I_0,
  output Out
);

  wire and_1_out, and_2_out, and_3_out, and_4_out, not_1_out, not_2_out, or_1_out, or_2_out;

  not not_1 (not_1_out, S_0);
  not not_2 (not_2_out, S_1);
  and and_1 (and_1_out, S_1, S_0, I_3);
  and and_2 (and_2_out, S_1, not_1_out, I_2);
  and and_3 (and_3_out, not_2_out, S_0, I_1);
  and and_4 (and_4_out, not_2_out, not_1_out, I_0);
  or or_1 (or_1_out, and_1_out, and_2_out);
  or or_2 (or_2_out, and_3_out, and_4_out);
  or or_3 (Out, or_1_out, or_2_out);
endmodule
