// Digital circuit 8Bit_2 to 1_Mux.dig as structural Verilog
module _8Bit_2_to_1_Mux (
  input  m_7,
  input  m_6,
  input  m_5,
  input  m_4,
  input  m_3,
  input  m_2,
  input  m_1,
  input  m_0,
  input  d_7,
  input  d_6,
  input  B_5,
  input  d_4,
  input  d_3,
  input  d_2,
  input  d_1,
  input  d_0,
  input  S_0,
  output Out_7,
  output Out_6,
  output Out_5,
  output Out_4,
  output Out_3,
  output Out_2,
  output Out_1,
  output Out_0
);

  _2_to_1_Mux _2_to_1_mux_1 (.I_1(d_0), .I_0(m_0), .S_0(S_0), .Out(Out_0));
  _2_to_1_Mux _2_to_1_mux_2 (.I_1(d_1), .I_0(m_1), .S_0(S_0), .Out(Out_1));
  _2_to_1_Mux _2_to_1_mux_3 (.I_1(d_2), .I_0(m_2), .S_0(S_0), .Out(Out_2));
  _2_to_1_Mux _2_to_1_mux_4 (.I_1(d_3), .I_0(m_3), .S_0(S_0), .Out(Out_3));
  _2_to_1_Mux _2_to_1_mux_5 (.I_1(d_4), .I_0(m_4), .S_0(S_0), .Out(Out_4));
  _2_to_1_Mux _2_to_1_mux_6 (.I_1(B_5), .I_0(m_5), .S_0(S_0), .Out(Out_5));
  _2_to_1_Mux _2_to_1_mux_7 (.I_1(d_6), .I_0(m_6), .S_0(S_0), .Out(Out_6));
  _2_to_1_Mux _2_to_1_mux_8 (.I_1(d_7), .I_0(m_7), .S_0(S_0), .Out(Out_7));
endmodule
