// Digital circuit 8Bit_4 to 1_Mux.dig as structural Verilog
module _8Bit_4_to_1_Mux (
  input  Not_7,
  input  Not_6,
  input  Not_5,
  input  Not_4,
  input  Not_3,
  input  Not_2,
  input  Not_2_2,
  input  Not_0,
  input  Xor_7,
  input  Xor_6,
  input  Xor_5,
  input  Xor_4,
  input  Xor_3,
  input  Xor_2,
  input  Xor_1,
  input  Xor_0,
  input  Or_7,
  input  Or_6,
  input  Or_5,
  input  Or_4,
  input  Or_3,
  input  Or_2,
  input  Or_1,
  input  Or_0,
  input  And_7,
  input  And_6,
  input  And_5,
  input  And_4,
  input  And_3,
  input  And_2,
  input  And_1,
  input  And_0,
  input  S_1,
  input  S_0,
  output Out_7,
  output Out_6,
  output Out_5,
  output Out_4,
  output Out_3,
  output Out_2,
  output Out_1,
  output Out_0
);

  _4_to_1_Mux _4_to_1_mux_1 (.S_1(S_1), .S_0(S_0), .I_3(Not_0), .I_2(Xor_0), .I_1(Or_0), .I_0(And_0), .Out(Out_0));
  _4_to_1_Mux _4_to_1_mux_2 (.S_1(S_1), .S_0(S_0), .I_3(Not_2_2), .I_2(Xor_1), .I_1(Or_1), .I_0(And_1), .Out(Out_1));
  _4_to_1_Mux _4_to_1_mux_3 (.S_1(S_1), .S_0(S_0), .I_3(Not_2), .I_2(Xor_2), .I_1(Or_2), .I_0(And_2), .Out(Out_2));
  _4_to_1_Mux _4_to_1_mux_4 (.S_1(S_1), .S_0(S_0), .I_3(Not_3), .I_2(Xor_3), .I_1(Or_3), .I_0(And_3), .Out(Out_3));
  _4_to_1_Mux _4_to_1_mux_5 (.S_1(S_1), .S_0(S_0), .I_3(Not_4), .I_2(Xor_4), .I_1(Or_4), .I_0(And_4), .Out(Out_4));
  _4_to_1_Mux _4_to_1_mux_6 (.S_1(S_1), .S_0(S_0), .I_3(Not_5), .I_2(Xor_5), .I_1(Or_5), .I_0(And_5), .Out(Out_5));
  _4_to_1_Mux _4_to_1_mux_7 (.S_1(S_1), .S_0(S_0), .I_3(Not_6), .I_2(Xor_6), .I_1(Or_6), .I_0(And_6), .Out(Out_6));
  _4_to_1_Mux _4_to_1_mux_8 (.S_1(S_1), .S_0(S_0), .I_3(Not_7), .I_2(Xor_7), .I_1(Or_7), .I_0(And_7), .Out(Out_7));
endmodule
