// Digital circuit 8Bit_Arthm.dig as structural Verilog
module _8Bit_Arthm (
  input  A_7,
  input  A_0,
  input  A_1,
  input  A_2,
  input  A_3,
  input  A_4,
  input  A_5,
  input  A_6,
  input  B_0,
  input  B_1,
  input  B_2,
  input  B_3,
  input  B_4,
  input  B_5,
  input  B_6,
  input  B_7,
  input  tgl,
  output S_0,
  output S_1,
  output S_2,
  output S_3,
  output S_4,
  output S_5,
  output S_6,
  output S_7,
  output Ovf,
  output _0__A_eq_B,
  output A_lt_B__ve,
  output A_gt_B
);

  wire _1bit_fulladder_1_c_out, _1bit_fulladder_2_c_out, _1bit_fulladder_3_c_out, _1bit_fulladder_4_c_out,
       _1bit_fulladder_5_c_out, _1bit_fulladder_6_c_out, _1bit_fulladder_7_c_out, _1bit_fulladder_8_c_out,
       nor_1_out, or_1_out, or_2_out, or_3_out, or_4_out, or_5_out, or_6_out, toggle_arthm_1_out_0,
       toggle_arthm_1_out_1, toggle_arthm_1_out_2, toggle_arthm_1_out_3, toggle_arthm_1_out_4,
       toggle_arthm_1_out_5, toggle_arthm_1_out_6, toggle_arthm_1_out_7, xor_2_out;

  Toggle_Arthm toggle_arthm_1 (
    .toggle(tgl), .IN_7(B_0), .IN_6(B_1), .IN_5(B_2), .IN_4(B_3), .IN_3(B_4), .IN_2(B_5), .IN_1(B_6),
    .IN_0(B_7), .OUT_7(toggle_arthm_1_out_7), .OUT_6(toggle_arthm_1_out_6), .OUT_5(toggle_arthm_1_out_5),
    .OUT_4(toggle_arthm_1_out_4), .OUT_3(toggle_arthm_1_out_3), .OUT_2(toggle_arthm_1_out_2),
    .OUT_1(toggle_arthm_1_out_1), .OUT_0(toggle_arthm_1_out_0));
  _1Bit_FullAdder _1bit_fulladder_1 (
    .A(A_0), .B(toggle_arthm_1_out_7), .C_in(tgl), .S(S_0), .C_out(_1bit_fulladder_1_c_out));
  _1Bit_FullAdder _1bit_fulladder_2 (
    .A(A_1), .B(toggle_arthm_1_out_6), .C_in(_1bit_fulladder_1_c_out), .S(S_1),
    .C_out(_1bit_fulladder_2_c_out));
  _1Bit_FullAdder _1bit_fulladder_3 (
    .A(A_2), .B(toggle_arthm_1_out_5), .C_in(_1bit_fulladder_2_c_out), .S(S_2),
    .C_out(_1bit_fulladder_3_c_out));
  _1Bit_FullAdder _1bit_fulladder_4 (
    .A(A_3), .B(toggle_arthm_1_out_4), .C_in(_1bit_fulladder_3_c_out), .S(S_3),
    .C_out(_1bit_fulladder_4_c_out));
  _1Bit_FullAdder _1bit_fulladder_5 (
    .A(A_4), .B(toggle_arthm_1_out_3), .C_in(_1bit_fulladder_4_c_out), .S(S_4),
    .C_out(_1bit_fulladder_5_c_out));
  _1Bit_FullAdder _1bit_fulladder_6 (
    .A(A_5), .B(toggle_arthm_1_out_2), .C_in(_1bit_fulladder_5_c_out), .S(S_5),
    .C_out(_1bit_fulladder_6_c_out));
  _1Bit_FullAdder _1bit_fulladder_7 (
    .A(A_6), .B(toggle_arthm_1_out_1), .C_in(_1bit_fulladder_6_c_out), .S(S_6),
    .C_out(_1bit_fulladder_7_c_out));
  _1Bit_FullAdder _1bit_fulladder_8 (
    .A(A_7), .B(toggle_arthm_1_out_0), .C_in(_1bit_fulladder_7_c_out), .S(S_7),
    .C_out(_1bit_fulladder_8_c_out));
  xor xor_1 (Ovf, _1bit_fulladder_8_c_out, _1bit_fulladder_7_c_out);
  nor nor_1 (nor_1_out, xor_2_out, _0__A_eq_B);
  xor xor_2 (xor_2_out, S_7, Ovf);
  and and_1 (A_gt_B, tgl, nor_1_out);
  or or_1 (or_1_out, S_0, S_1);
  or or_2 (or_2_out, S_2, S_3);
  or or_3 (or_3_out, S_4, S_5);
  or or_4 (or_4_out, S_6, S_7);
  and and_2 (A_lt_B__ve, xor_2_out, tgl);
  or or_5 (or_5_out, or_1_out, or_2_out);
  or or_6 (or_6_out, or_3_out, or_4_out);
  nor nor_2 (_0__A_eq_B, or_6_out, or_5_out);
endmodule
