// Digital circuit BitWise_Oprtn.dig as structural Verilog
module BitWise_Oprtn (
  input  A_7,
  input  A_6,
  input  A_5,
  input  A_4,
  input  A_3,
  input  A_2,
  input  A_1,
  input  A_0,
  input  B_7,
  input  B_6,
  input  B_5,
  input  B_4,
  input  B_3,
  input  B_2,
  input  B_1,
  input  B_0,
  input  S_1,
  input  S_0,
  output Out_7,
  output Out_6,
  output Out_5,
  output Out_4,
  output Out_3,
  output Out_2,
  output Out_1,
  output Out_0
);

  wire and_1_out, and_2_out, and_3_out, and_4_out, and_5_out, and_6_out, and_7_out, and_8_out, not_1_out,
       not_2_out, not_3_out, not_4_out, not_5_out, not_6_out, not_7_out, not_8_out, or_1_out, or_2_out,
       or_3_out, or_4_out, or_5_out, or_6_out, or_7_out, or_8_out, xor_1_out, xor_2_out, xor_3_out,
       xor_4_out, xor_5_out, xor_6_out, xor_7_out, xor_8_out;

  not not_1 (not_1_out, A_7);
  not not_2 (not_2_out, A_6);
  not not_3 (not_3_out, A_5);
  not not_4 (not_4_out, A_4);
  not not_5 (not_5_out, A_3);
  not not_6 (not_6_out, A_2);
  not not_7 (not_7_out, A_1);
  not not_8 (not_8_out, A_0);
  xor xor_1 (xor_1_out, A_7, B_7);
  xor xor_2 (xor_2_out, A_6, B_6);
  xor xor_3 (xor_3_out, A_5, B_5);
  xor xor_4 (xor_4_out, A_4, B_4);
  xor xor_5 (xor_5_out, A_3, B_3);
  xor xor_6 (xor_6_out, A_2, B_2);
  xor xor_7 (xor_7_out, A_1, B_1);
  xor xor_8 (xor_8_out, A_0, B_0);
  or or_1 (or_1_out, A_7, B_7);
  or or_2 (or_2_out, A_6, B_6);
  or or_3 (or_3_out, A_5, B_5);
  or or_4 (or_4_out, A_4, B_4);
  or or_5 (or_5_out, A_3, B_3);
  or or_6 (or_6_out, A_2, B_2);
  or or_7 (or_7_out, A_1, B_1);
  or or_8 (or_8_out, A_0, B_0);
  and and_1 (and_1_out, A_7, B_7);
  and and_2 (and_2_out, A_6, B_6);
  and and_3 (and_3_out, A_5, B_5);
  and and_4 (and_4_out, A_4, B_4);
  and and_5 (and_5_out, A_3, B_3);
  and and_6 (and_6_out, A_2, B_2);
  and and_7 (and_7_out, A_1, B_1);
  and and_8 (and_8_out, A_0, B_0);
  _8Bit_4_to_1_Mux _8bit_4_to_1_mux_1 (
    .Not_7(not_1_out), .Not_6(not_2_out), .Not_5(not_3_out), .Not_4(not_4_out), .Not_3(not_5_out),
    .Not_2(not_6_out), .Not_2_2(not_7_out), .Not_0(not_8_out), .Xor_7(xor_1_out), .Xor_6(xor_2_out),
    .Xor_5(xor_3_out), .Xor_4(xor_4_out), .Xor_3(xor_5_out), .Xor_2(xor_6_out), .Xor_1(xor_7_out),
    .Xor_0(xor_8_out), .Or_7(or_1_out), .Or_6(or_2_out), .Or_5(or_3_out), .Or_4(or_4_out), .Or_3(or_5_out),
    .Or_2(or_6_out), .Or_1(or_7_out), .Or_0(or_8_out), .And_7(and_1_out), .And_6(and_2_out),
    .And_5(and_3_out), .And_4(and_4_out), .And_3(and_5_out), .And_2(and_6_out), .And_1(and_7_out),
    .And_0(and_8_out), .S_1(S_1), .S_0(S_0), .Out_7(Out_7), .Out_6(Out_6), .Out_5(Out_5), .Out_4(Out_4),
    .Out_3(Out_3), .Out_2(Out_2), .Out_1(Out_1), .Out_0(Out_0));
endmodule
