// Digital circuit Program_Counter.dig as structural Verilog
module Program_Counter (
  input  Jmp,
  input  Clk,
  input  Wrt,
  input  Rd,
  input  J_0,
  input  J_1,
  input  J_2,
  input  J_3,
  input  J_4,
  input  J_5,
  input  J_6,
  input  J_7,
  input  J_8,
  input  J_9,
  input  J_10,
  input  J_11,
  input  J_12,
  input  J_13,
  input  J_14,
  input  J_15,
  output C_0,
  output C_1,
  output C_2,
  output C_3,
  output C_4,
  output C_5,
  output C_6,
  output C_7,
  output C_8,
  output C_9,
  output C_10,
  output C_11,
  output C_12,
  output C_13,
  output C_14,
  output C_15
);

  wire _1bit_fulladder_1_c_out, _1bit_fulladder_1_s, _1bit_fulladder_2_c_out, _1bit_fulladder_2_s,
       _1bit_fulladder_3_c_out, _1bit_fulladder_3_s, _1bit_fulladder_4_c_out, _1bit_fulladder_4_s,
       _1bit_fulladder_5_c_out, _1bit_fulladder_5_s, _1bit_fulladder_6_c_out, _1bit_fulladder_6_s,
       _1bit_fulladder_7_c_out, _1bit_fulladder_7_s, _1bit_fulladder_8_c_out, _1bit_fulladder_8_s,
       _1bit_fulladder_9_c_out, _1bit_fulladder_9_s, _1bit_fulladder_10_c_out, _1bit_fulladder_10_s,
       _1bit_fulladder_11_c_out, _1bit_fulladder_11_s, _1bit_fulladder_12_c_out, _1bit_fulladder_12_s,
       _1bit_fulladder_13_c_out, _1bit_fulladder_13_s, _1bit_fulladder_14_c_out, _1bit_fulladder_14_s,
       _1bit_fulladder_15_c_out, _1bit_fulladder_15_s, _1bit_fulladder_16_s, _8bit_2_to_1_mux_1_out_0,
       _8bit_2_to_1_mux_1_out_1, _8bit_2_to_1_mux_1_out_2, _8bit_2_to_1_mux_1_out_3,
       _8bit_2_to_1_mux_1_out_4, _8bit_2_to_1_mux_1_out_5, _8bit_2_to_1_mux_1_out_6,
       _8bit_2_to_1_mux_1_out_7, _8bit_2_to_1_mux_2_out_0, _8bit_2_to_1_mux_2_out_1,
       _8bit_2_to_1_mux_2_out_2, _8bit_2_to_1_mux_2_out_3, _8bit_2_to_1_mux_2_out_4,
       _8bit_2_to_1_mux_2_out_5, _8bit_2_to_1_mux_2_out_6, _8bit_2_to_1_mux_2_out_7;

  _8Bit_2_to_1_Mux _8bit_2_to_1_mux_1 (
    .m_7(_1bit_fulladder_8_s), .m_6(_1bit_fulladder_7_s), .m_5(_1bit_fulladder_6_s),
    .m_4(_1bit_fulladder_5_s), .m_3(_1bit_fulladder_4_s), .m_2(_1bit_fulladder_3_s),
    .m_1(_1bit_fulladder_2_s), .m_0(_1bit_fulladder_1_s), .d_7(J_7), .d_6(J_6), .B_5(J_5), .d_4(J_4),
    .d_3(J_3), .d_2(J_2), .d_1(J_1), .d_0(J_0), .S_0(Jmp), .Out_7(_8bit_2_to_1_mux_1_out_7),
    .Out_6(_8bit_2_to_1_mux_1_out_6), .Out_5(_8bit_2_to_1_mux_1_out_5), .Out_4(_8bit_2_to_1_mux_1_out_4),
    .Out_3(_8bit_2_to_1_mux_1_out_3), .Out_2(_8bit_2_to_1_mux_1_out_2), .Out_1(_8bit_2_to_1_mux_1_out_1),
    .Out_0(_8bit_2_to_1_mux_1_out_0));
  _8Bit_2_to_1_Mux _8bit_2_to_1_mux_2 (
    .m_7(_1bit_fulladder_16_s), .m_6(_1bit_fulladder_15_s), .m_5(_1bit_fulladder_14_s),
    .m_4(_1bit_fulladder_13_s), .m_3(_1bit_fulladder_12_s), .m_2(_1bit_fulladder_11_s),
    .m_1(_1bit_fulladder_10_s), .m_0(_1bit_fulladder_9_s), .d_7(J_15), .d_6(J_14), .B_5(J_13), .d_4(J_12),
    .d_3(J_11), .d_2(J_10), .d_1(J_9), .d_0(J_8), .S_0(Jmp), .Out_7(_8bit_2_to_1_mux_2_out_7),
    .Out_6(_8bit_2_to_1_mux_2_out_6), .Out_5(_8bit_2_to_1_mux_2_out_5), .Out_4(_8bit_2_to_1_mux_2_out_4),
    .Out_3(_8bit_2_to_1_mux_2_out_3), .Out_2(_8bit_2_to_1_mux_2_out_2), .Out_1(_8bit_2_to_1_mux_2_out_1),
    .Out_0(_8bit_2_to_1_mux_2_out_0));
  _16bit_Reg _16bit_reg_1 (
    .In_1(_8bit_2_to_1_mux_1_out_0), .Clk(Clk), .Wrt(Wrt), .In_2(_8bit_2_to_1_mux_1_out_1),
    .In_3(_8bit_2_to_1_mux_1_out_2), .In_4(_8bit_2_to_1_mux_1_out_3), .In_5(_8bit_2_to_1_mux_1_out_4),
    .In_6(_8bit_2_to_1_mux_1_out_5), .In_7(_8bit_2_to_1_mux_1_out_6), .In_8(_8bit_2_to_1_mux_1_out_7),
    .In_9(_8bit_2_to_1_mux_2_out_0), .In_10(_8bit_2_to_1_mux_2_out_1), .In_11(_8bit_2_to_1_mux_2_out_2),
    .In_12(_8bit_2_to_1_mux_2_out_3), .In_13(_8bit_2_to_1_mux_2_out_4), .In_14(_8bit_2_to_1_mux_2_out_5),
    .In_15(_8bit_2_to_1_mux_2_out_6), .In_16(_8bit_2_to_1_mux_2_out_7), .Rd(Rd), .Out_1(C_0), .Out_2(C_1),
    .Out_3(C_2), .Out_4(C_3), .Out_5(C_4), .Out_6(C_5), .Out_7(C_6), .Out_8(C_7), .Out_9(C_8), .Out_10(C_9),
    .Out_11(C_10), .Out_12(C_11), .Out_13(C_12), .Out_14(C_13), .Out_15(C_14), .Out_16(C_15));
  _1Bit_FullAdder _1bit_fulladder_1 (
    .A(C_0), .B(1'b1), .C_in(1'b0), .S(_1bit_fulladder_1_s), .C_out(_1bit_fulladder_1_c_out));
  _1Bit_FullAdder _1bit_fulladder_2 (
    .A(C_1), .B(1'b0), .C_in(_1bit_fulladder_1_c_out), .S(_1bit_fulladder_2_s),
    .C_out(_1bit_fulladder_2_c_out));
  _1Bit_FullAdder _1bit_fulladder_3 (
    .A(C_2), .B(1'b0), .C_in(_1bit_fulladder_2_c_out), .S(_1bit_fulladder_3_s),
    .C_out(_1bit_fulladder_3_c_out));
  _1Bit_FullAdder _1bit_fulladder_4 (
    .A(C_3), .B(1'b0), .C_in(_1bit_fulladder_3_c_out), .S(_1bit_fulladder_4_s),
    .C_out(_1bit_fulladder_4_c_out));
  _1Bit_FullAdder _1bit_fulladder_5 (
    .A(C_4), .B(1'b0), .C_in(_1bit_fulladder_4_c_out), .S(_1bit_fulladder_5_s),
    .C_out(_1bit_fulladder_5_c_out));
  _1Bit_FullAdder _1bit_fulladder_6 (
    .A(C_5), .B(1'b0), .C_in(_1bit_fulladder_5_c_out), .S(_1bit_fulladder_6_s),
    .C_out(_1bit_fulladder_6_c_out));
  _1Bit_FullAdder _1bit_fulladder_7 (
    .A(C_6), .B(1'b0), .C_in(_1bit_fulladder_6_c_out), .S(_1bit_fulladder_7_s),
    .C_out(_1bit_fulladder_7_c_out));
  _1Bit_FullAdder _1bit_fulladder_8 (
    .A(C_7), .B(1'b0), .C_in(_1bit_fulladder_7_c_out), .S(_1bit_fulladder_8_s),
    .C_out(_1bit_fulladder_8_c_out));
  _1Bit_FullAdder _1bit_fulladder_9 (
    .A(C_8), .B(1'b0), .C_in(_1bit_fulladder_8_c_out), .S(_1bit_fulladder_9_s),
    .C_out(_1bit_fulladder_9_c_out));
  _1Bit_FullAdder _1bit_fulladder_10 (
    .A(C_9), .B(1'b0), .C_in(_1bit_fulladder_9_c_out), .S(_1bit_fulladder_10_s),
    .C_out(_1bit_fulladder_10_c_out));
  _1Bit_FullAdder _1bit_fulladder_11 (
    .A(C_10), .B(1'b0), .C_in(_1bit_fulladder_10_c_out), .S(_1bit_fulladder_11_s),
    .C_out(_1bit_fulladder_11_c_out));
  _1Bit_FullAdder _1bit_fulladder_12 (
    .A(C_11), .B(1'b0), .C_in(_1bit_fulladder_11_c_out), .S(_1bit_fulladder_12_s),
    .C_out(_1bit_fulladder_12_c_out));
  _1Bit_FullAdder _1bit_fulladder_13 (
    .A(C_12), .B(1'b0), .C_in(_1bit_fulladder_12_c_out), .S(_1bit_fulladder_13_s),
    .C_out(_1bit_fulladder_13_c_out));
  _1Bit_FullAdder _1bit_fulladder_14 (
    .A(C_13), .B(1'b0), .C_in(_1bit_fulladder_13_c_out), .S(_1bit_fulladder_14_s),
    .C_out(_1bit_fulladder_14_c_out));
  _1Bit_FullAdder _1bit_fulladder_15 (
    .A(C_14), .B(1'b0), .C_in(_1bit_fulladder_14_c_out), .S(_1bit_fulladder_15_s),
    .C_out(_1bit_fulladder_15_c_out));
  _1Bit_FullAdder _1bit_fulladder_16 (
    .A(C_15), .B(1'b0), .C_in(_1bit_fulladder_15_c_out), .S(_1bit_fulladder_16_s));  // open: C_out
endmodule
