// Digital circuit Shifter.dig as structural Verilog
module Shifter (
  input  In_3,
  input  In_2,
  input  In_1,
  input  In_0,
  input  In_7,
  input  In_6,
  input  In_5,
  input  In_4,
  input  S_0,
  output Out_7,
  output Out_6,
  output Out_5,
  output Out_4,
  output Out_3,
  output Out_2,
  output Out_1,
  output Out_0,
  output M_Ovf,
  output Rmdr
);

  wire _2_to_1_mux_1_out;

  _8Bit_2_to_1_Mux _8bit_2_to_1_mux_1 (
    .m_7(In_6), .m_6(In_5), .m_5(In_4), .m_4(In_3), .m_3(In_2), .m_2(In_1), .m_1(In_0), .m_0(1'b0),
    .d_7(1'b0), .d_6(In_7), .B_5(In_6), .d_4(In_5), .d_3(In_4), .d_2(In_3), .d_1(In_2), .d_0(In_1),
    .S_0(S_0), .Out_7(Out_7), .Out_6(Out_6), .Out_5(Out_5), .Out_4(Out_4), .Out_3(Out_3), .Out_2(Out_2),
    .Out_1(Out_1), .Out_0(Out_0));
  _2_to_1_Mux _2_to_1_mux_1 (.I_1(In_0), .I_0(In_7), .S_0(S_0), .Out(_2_to_1_mux_1_out));
  and and_1 (M_Ovf, _2_to_1_mux_1_out, In_7);
  and and_2 (Rmdr, _2_to_1_mux_1_out, In_0);
endmodule
