// Digital circuit Toggle_Arthm.dig as structural Verilog
module Toggle_Arthm (
  input  toggle,
  input  IN_7,
  input  IN_6,
  input  IN_5,
  input  IN_4,
  input  IN_3,
  input  IN_2,
  input  IN_1,
  input  IN_0,
  output OUT_7,
  output OUT_6,
  output OUT_5,
  output OUT_4,
  output OUT_3,
  output OUT_2,
  output OUT_1,
  output OUT_0
);

  xor xor_1 (OUT_0, IN_0, toggle);
  xor xor_2 (OUT_1, IN_1, toggle);
  xor xor_3 (OUT_2, IN_2, toggle);
  xor xor_4 (OUT_3, IN_3, toggle);
  xor xor_5 (OUT_4, IN_4, toggle);
  xor xor_6 (OUT_5, IN_5, toggle);
  xor xor_7 (OUT_6, IN_6, toggle);
  xor xor_8 (OUT_7, IN_7, toggle);
endmodule
