// Digital circuit 2 to 1_Mux.dig as structural Verilog
module _2_to_1_Mux (
  input  I_1,
  input  I_0,
  input  S_0,
  output Out
);

  wire and_1_out, and_2_out, not_1_out;

  not not_1 (not_1_out, S_0);
  and and_1 (and_1_out, I_1, S_0);
  and and_2 (and_2_out, I_0, not_1_out);
  or or_1 (Out, and_1_out, and_2_out);
endmodule
