// Digital circuit ALU.dig as structural Verilog
module ALU (
  input  B_7,
  input  B_6,
  input  B_5,
  input  B_4,
  input  B_3,
  input  B_2,
  input  B_1,
  input  B_0,
  input  A_7,
  input  A_6,
  input  A_5,
  input  A_4,
  input  A_3,
  input  A_2,
  input  A_1,
  input  A_0,
  input  D_5,
  input  D_4,
  input  D_3,
  input  D_2,
  input  D_1,
  input  D_0,
  input  D_6,
  input  D_7,
  output Out_7,
  output Out_6,
  output Out_5,
  output Out_4,
  output Out_3,
  output Out_2,
  output Out_1,
  output Out_0,
  output Ovf,
  output _0_A_eq_B,
  output ve_A_lt_B,
  output A_gt_B,
  output M_Ovf,
  output Rmdr
);

  wire _8bit_2_to_1_mux_1_out_0, _8bit_2_to_1_mux_1_out_1, _8bit_2_to_1_mux_1_out_2,
       _8bit_2_to_1_mux_1_out_3, _8bit_2_to_1_mux_1_out_4, _8bit_2_to_1_mux_1_out_5,
       _8bit_2_to_1_mux_1_out_6, _8bit_2_to_1_mux_1_out_7, _8bit_2_to_1_mux_2_out_0,
       _8bit_2_to_1_mux_2_out_1, _8bit_2_to_1_mux_2_out_2, _8bit_2_to_1_mux_2_out_3,
       _8bit_2_to_1_mux_2_out_4, _8bit_2_to_1_mux_2_out_5, _8bit_2_to_1_mux_2_out_6,
       _8bit_2_to_1_mux_2_out_7, _8bit_fulladder_1_p18, _8bit_fulladder_1_p19, _8bit_fulladder_1_p20,
       _8bit_fulladder_1_p21, _8bit_fulladder_1_p22, _8bit_fulladder_1_p23, _8bit_fulladder_1_p24,
       _8bit_fulladder_1_p25, bitwise_oprtn_1_out_0, bitwise_oprtn_1_out_1, bitwise_oprtn_1_out_2,
       bitwise_oprtn_1_out_3, bitwise_oprtn_1_out_4, bitwise_oprtn_1_out_5, bitwise_oprtn_1_out_6,
       bitwise_oprtn_1_out_7, shifter_1_out_0, shifter_1_out_1, shifter_1_out_2, shifter_1_out_3,
       shifter_1_out_4, shifter_1_out_5, shifter_1_out_6, shifter_1_out_7;

  // _8Bit_FullAdder _8bit_fulladder_1: pin names not known; wires that end beside it: A_7, A_0, A_1, A_2, A_3, A_4, A_5, A_6, B_0, B_1, B_2, B_3, B_4, B_5, B_6, B_7, D_6, _8bit_fulladder_1_p18, _8bit_fulladder_1_p19, _8bit_fulladder_1_p20, _8bit_fulladder_1_p21, _8bit_fulladder_1_p22, _8bit_fulladder_1_p23, _8bit_fulladder_1_p24, _8bit_fulladder_1_p25, Ovf, _0_A_eq_B, ve_A_lt_B, A_gt_B
  BitWise_Oprtn bitwise_oprtn_1 (
    .A_7(A_7), .A_6(A_6), .A_5(A_5), .A_4(A_4), .A_3(A_3), .A_2(A_2), .A_1(A_1), .A_0(A_0), .B_7(B_7),
    .B_6(B_6), .B_5(B_5), .B_4(B_4), .B_3(B_3), .B_2(B_2), .B_1(B_1), .B_0(B_0), .S_1(D_5), .S_0(D_4),
    .Out_7(bitwise_oprtn_1_out_7), .Out_6(bitwise_oprtn_1_out_6), .Out_5(bitwise_oprtn_1_out_5),
    .Out_4(bitwise_oprtn_1_out_4), .Out_3(bitwise_oprtn_1_out_3), .Out_2(bitwise_oprtn_1_out_2),
    .Out_1(bitwise_oprtn_1_out_1), .Out_0(bitwise_oprtn_1_out_0));
  _8Bit_2_to_1_Mux _8bit_2_to_1_mux_1 (
    .m_7(_8bit_fulladder_1_p25), .m_6(_8bit_fulladder_1_p24), .m_5(_8bit_fulladder_1_p23),
    .m_4(_8bit_fulladder_1_p22), .m_3(_8bit_fulladder_1_p21), .m_2(_8bit_fulladder_1_p20),
    .m_1(_8bit_fulladder_1_p19), .m_0(_8bit_fulladder_1_p18), .d_7(bitwise_oprtn_1_out_7),
    .d_6(bitwise_oprtn_1_out_6), .B_5(bitwise_oprtn_1_out_5), .d_4(bitwise_oprtn_1_out_4),
    .d_3(bitwise_oprtn_1_out_3), .d_2(bitwise_oprtn_1_out_2), .d_1(bitwise_oprtn_1_out_1),
    .d_0(bitwise_oprtn_1_out_0), .S_0(D_3), .Out_7(_8bit_2_to_1_mux_1_out_7),
    .Out_6(_8bit_2_to_1_mux_1_out_6), .Out_5(_8bit_2_to_1_mux_1_out_5), .Out_4(_8bit_2_to_1_mux_1_out_4),
    .Out_3(_8bit_2_to_1_mux_1_out_3), .Out_2(_8bit_2_to_1_mux_1_out_2), .Out_1(_8bit_2_to_1_mux_1_out_1),
    .Out_0(_8bit_2_to_1_mux_1_out_0));
  Shifter shifter_1 (
    .In_3(_8bit_2_to_1_mux_1_out_3), .In_2(_8bit_2_to_1_mux_1_out_2), .In_1(_8bit_2_to_1_mux_1_out_1),
    .In_0(_8bit_2_to_1_mux_1_out_0), .In_7(_8bit_2_to_1_mux_1_out_7), .In_6(_8bit_2_to_1_mux_1_out_6),
    .In_5(_8bit_2_to_1_mux_1_out_5), .In_4(_8bit_2_to_1_mux_1_out_4), .S_0(D_2), .Out_7(shifter_1_out_7),
    .Out_6(shifter_1_out_6), .Out_5(shifter_1_out_5), .Out_4(shifter_1_out_4), .Out_3(shifter_1_out_3),
    .Out_2(shifter_1_out_2), .Out_1(shifter_1_out_1), .Out_0(shifter_1_out_0), .M_Ovf(M_Ovf), .Rmdr(Rmdr));
  _8Bit_2_to_1_Mux _8bit_2_to_1_mux_2 (
    .m_7(_8bit_fulladder_1_p25), .m_6(_8bit_fulladder_1_p24), .m_5(_8bit_fulladder_1_p23),
    .m_4(_8bit_fulladder_1_p22), .m_3(_8bit_fulladder_1_p21), .m_2(_8bit_fulladder_1_p20),
    .m_1(_8bit_fulladder_1_p19), .m_0(_8bit_fulladder_1_p18), .d_7(shifter_1_out_7), .d_6(shifter_1_out_6),
    .B_5(shifter_1_out_5), .d_4(shifter_1_out_4), .d_3(shifter_1_out_3), .d_2(shifter_1_out_2),
    .d_1(shifter_1_out_1), .d_0(shifter_1_out_0), .S_0(D_1), .Out_7(_8bit_2_to_1_mux_2_out_7),
    .Out_6(_8bit_2_to_1_mux_2_out_6), .Out_5(_8bit_2_to_1_mux_2_out_5), .Out_4(_8bit_2_to_1_mux_2_out_4),
    .Out_3(_8bit_2_to_1_mux_2_out_3), .Out_2(_8bit_2_to_1_mux_2_out_2), .Out_1(_8bit_2_to_1_mux_2_out_1),
    .Out_0(_8bit_2_to_1_mux_2_out_0));
  _8Bit_2_to_1_Mux _8bit_2_to_1_mux_3 (
    .m_7(_8bit_2_to_1_mux_2_out_7), .m_6(_8bit_2_to_1_mux_2_out_6), .m_5(_8bit_2_to_1_mux_2_out_5),
    .m_4(_8bit_2_to_1_mux_2_out_4), .m_3(_8bit_2_to_1_mux_2_out_3), .m_2(_8bit_2_to_1_mux_2_out_2),
    .m_1(_8bit_2_to_1_mux_2_out_1), .m_0(_8bit_2_to_1_mux_2_out_0), .d_7(bitwise_oprtn_1_out_7),
    .d_6(bitwise_oprtn_1_out_6), .B_5(bitwise_oprtn_1_out_5), .d_4(bitwise_oprtn_1_out_4),
    .d_3(bitwise_oprtn_1_out_3), .d_2(bitwise_oprtn_1_out_2), .d_1(bitwise_oprtn_1_out_1),
    .d_0(bitwise_oprtn_1_out_0), .S_0(D_0), .Out_7(Out_7), .Out_6(Out_6), .Out_5(Out_5), .Out_4(Out_4),
    .Out_3(Out_3), .Out_2(Out_2), .Out_1(Out_1), .Out_0(Out_0));
endmodule
