// Digital circuit Stack_Pointer.dig as structural Verilog
module Stack_Pointer (
  input  Clk,
  input  S_1,
  input  S_0,
  input  L_0,
  input  L_1,
  input  L_2,
  input  L_3,
  input  L_4,
  input  L_5,
  input  L_6,
  input  L_7,
  input  L_8,
  input  L_9,
  input  L_10,
  input  L_11,
  input  L_12,
  input  L_13,
  input  L_14,
  input  L_15,
  output Out_0,
  output Out_1,
  output Out_2,
  output Out_3,
  output Out_4,
  output Out_5,
  output Out_6,
  output Out_7,
  output Out_8,
  output Out_9,
  output Out_10,
  output Out_11,
  output Out_12,
  output Out_13,
  output Out_14,
  output Out_15
);

  wire _1bit_fulladder_1_c_out, _1bit_fulladder_1_s, _1bit_fulladder_2_c_out, _1bit_fulladder_2_s,
       _1bit_fulladder_3_c_out, _1bit_fulladder_3_s, _1bit_fulladder_4_c_out, _1bit_fulladder_4_s,
       _1bit_fulladder_5_c_out, _1bit_fulladder_5_s, _1bit_fulladder_6_c_out, _1bit_fulladder_6_s,
       _1bit_fulladder_7_c_out, _1bit_fulladder_7_s, _1bit_fulladder_8_c_out, _1bit_fulladder_8_s,
       _1bit_fulladder_9_c_out, _1bit_fulladder_9_s, _1bit_fulladder_10_c_out, _1bit_fulladder_10_s,
       _1bit_fulladder_11_c_out, _1bit_fulladder_11_s, _1bit_fulladder_12_c_out, _1bit_fulladder_12_s,
       _1bit_fulladder_13_c_out, _1bit_fulladder_13_s, _1bit_fulladder_14_c_out, _1bit_fulladder_14_s,
       _1bit_fulladder_15_c_out, _1bit_fulladder_15_s, _1bit_fulladder_16_s, _16bit_2_to_1_mux_1_out_0,
       _16bit_2_to_1_mux_1_out_1, _16bit_2_to_1_mux_1_out_2, _16bit_2_to_1_mux_1_out_3,
       _16bit_2_to_1_mux_1_out_4, _16bit_2_to_1_mux_1_out_5, _16bit_2_to_1_mux_1_out_6,
       _16bit_2_to_1_mux_1_out_7, _16bit_2_to_1_mux_1_out_8, _16bit_2_to_1_mux_1_out_9,
       _16bit_2_to_1_mux_1_out_10, _16bit_2_to_1_mux_1_out_11, _16bit_2_to_1_mux_1_out_12,
       _16bit_2_to_1_mux_1_out_13, _16bit_2_to_1_mux_1_out_14, _16bit_2_to_1_mux_1_out_15,
       _16bit_2_to_1_mux_2_out_0, _16bit_2_to_1_mux_2_out_1, _16bit_2_to_1_mux_2_out_2,
       _16bit_2_to_1_mux_2_out_3, _16bit_2_to_1_mux_2_out_4, _16bit_2_to_1_mux_2_out_5,
       _16bit_2_to_1_mux_2_out_6, _16bit_2_to_1_mux_2_out_7, _16bit_2_to_1_mux_2_out_8,
       _16bit_2_to_1_mux_2_out_9, _16bit_2_to_1_mux_2_out_10, _16bit_2_to_1_mux_2_out_11,
       _16bit_2_to_1_mux_2_out_12, _16bit_2_to_1_mux_2_out_13, _16bit_2_to_1_mux_2_out_14,
       _16bit_2_to_1_mux_2_out_15;

  _16Bit_2_to_1_Mux _16bit_2_to_1_mux_1 (
    .S_0(S_0), .A_0(_1bit_fulladder_1_s), .A_1(_1bit_fulladder_2_s), .A_2(_1bit_fulladder_3_s),
    .A_3(_1bit_fulladder_4_s), .A_4(_1bit_fulladder_5_s), .A_5(_1bit_fulladder_6_s),
    .A_6(_1bit_fulladder_7_s), .A_7(_1bit_fulladder_8_s), .A_8(_1bit_fulladder_9_s),
    .A_9(_1bit_fulladder_10_s), .A_10(_1bit_fulladder_11_s), .A_11(_1bit_fulladder_12_s),
    .A_12(_1bit_fulladder_13_s), .A_13(_1bit_fulladder_14_s), .A_14(_1bit_fulladder_15_s),
    .A_15(_1bit_fulladder_16_s), .B_0(L_0), .B_1(L_1), .B_2(L_2), .B_3(L_3), .B_4(L_4), .B_5(L_5), .B_6(L_6),
    .B_7(L_7), .B_8(L_8), .B_9(L_9), .B_10(L_10), .B_11(L_11), .B_12(L_12), .B_13(L_13), .B_14(L_14),
    .B_15(L_15), .Out_0(_16bit_2_to_1_mux_1_out_0), .Out_1(_16bit_2_to_1_mux_1_out_1),
    .Out_2(_16bit_2_to_1_mux_1_out_2), .Out_3(_16bit_2_to_1_mux_1_out_3), .Out_4(_16bit_2_to_1_mux_1_out_4),
    .Out_5(_16bit_2_to_1_mux_1_out_5), .Out_6(_16bit_2_to_1_mux_1_out_6), .Out_7(_16bit_2_to_1_mux_1_out_7),
    .Out_8(_16bit_2_to_1_mux_1_out_8), .Out_9(_16bit_2_to_1_mux_1_out_9),
    .Out_10(_16bit_2_to_1_mux_1_out_10), .Out_11(_16bit_2_to_1_mux_1_out_11),
    .Out_12(_16bit_2_to_1_mux_1_out_12), .Out_13(_16bit_2_to_1_mux_1_out_13),
    .Out_14(_16bit_2_to_1_mux_1_out_14), .Out_15(_16bit_2_to_1_mux_1_out_15));
  _16bit_Reg _16bit_reg_1 (
    .In_1(_16bit_2_to_1_mux_1_out_0), .Clk(Clk), .Wrt(1'b1), .In_2(_16bit_2_to_1_mux_1_out_1),
    .In_3(_16bit_2_to_1_mux_1_out_2), .In_4(_16bit_2_to_1_mux_1_out_3), .In_5(_16bit_2_to_1_mux_1_out_4),
    .In_6(_16bit_2_to_1_mux_1_out_5), .In_7(_16bit_2_to_1_mux_1_out_6), .In_8(_16bit_2_to_1_mux_1_out_7),
    .In_9(_16bit_2_to_1_mux_1_out_8), .In_10(_16bit_2_to_1_mux_1_out_9), .In_11(_16bit_2_to_1_mux_1_out_10),
    .In_12(_16bit_2_to_1_mux_1_out_11), .In_13(_16bit_2_to_1_mux_1_out_12),
    .In_14(_16bit_2_to_1_mux_1_out_13), .In_15(_16bit_2_to_1_mux_1_out_14),
    .In_16(_16bit_2_to_1_mux_1_out_15), .Rd(1'b1), .Out_1(Out_0), .Out_2(Out_1), .Out_3(Out_2),
    .Out_4(Out_3), .Out_5(Out_4), .Out_6(Out_5), .Out_7(Out_6), .Out_8(Out_7), .Out_9(Out_8), .Out_10(Out_9),
    .Out_11(Out_10), .Out_12(Out_11), .Out_13(Out_12), .Out_14(Out_13), .Out_15(Out_14), .Out_16(Out_15));
  _16Bit_2_to_1_Mux _16bit_2_to_1_mux_2 (
    .S_0(S_1), .A_0(1'b1), .A_1(1'b0), .A_2(1'b0), .A_3(1'b0), .A_4(1'b0), .A_5(1'b0), .A_6(1'b0),
    .A_7(1'b0), .A_8(1'b0), .A_9(1'b0), .A_10(1'b0), .A_11(1'b0), .A_12(1'b0), .A_13(1'b0), .A_14(1'b0),
    .A_15(1'b0), .B_0(1'b1), .B_1(1'b1), .B_2(1'b1), .B_3(1'b1), .B_4(1'b1), .B_5(1'b1), .B_6(1'b1),
    .B_7(1'b1), .B_8(1'b1), .B_9(1'b1), .B_10(1'b1), .B_11(1'b1), .B_12(1'b1), .B_13(1'b1), .B_14(1'b1),
    .B_15(1'b1), .Out_0(_16bit_2_to_1_mux_2_out_0), .Out_1(_16bit_2_to_1_mux_2_out_1),
    .Out_2(_16bit_2_to_1_mux_2_out_2), .Out_3(_16bit_2_to_1_mux_2_out_3), .Out_4(_16bit_2_to_1_mux_2_out_4),
    .Out_5(_16bit_2_to_1_mux_2_out_5), .Out_6(_16bit_2_to_1_mux_2_out_6), .Out_7(_16bit_2_to_1_mux_2_out_7),
    .Out_8(_16bit_2_to_1_mux_2_out_8), .Out_9(_16bit_2_to_1_mux_2_out_9),
    .Out_10(_16bit_2_to_1_mux_2_out_10), .Out_11(_16bit_2_to_1_mux_2_out_11),
    .Out_12(_16bit_2_to_1_mux_2_out_12), .Out_13(_16bit_2_to_1_mux_2_out_13),
    .Out_14(_16bit_2_to_1_mux_2_out_14), .Out_15(_16bit_2_to_1_mux_2_out_15));
  _1Bit_FullAdder _1bit_fulladder_1 (
    .A(Out_0), .B(_16bit_2_to_1_mux_2_out_0), .C_in(1'b0), .S(_1bit_fulladder_1_s),
    .C_out(_1bit_fulladder_1_c_out));
  _1Bit_FullAdder _1bit_fulladder_2 (
    .A(Out_1), .B(_16bit_2_to_1_mux_2_out_1), .C_in(_1bit_fulladder_1_c_out), .S(_1bit_fulladder_2_s),
    .C_out(_1bit_fulladder_2_c_out));
  _1Bit_FullAdder _1bit_fulladder_3 (
    .A(Out_2), .B(_16bit_2_to_1_mux_2_out_2), .C_in(_1bit_fulladder_2_c_out), .S(_1bit_fulladder_3_s),
    .C_out(_1bit_fulladder_3_c_out));
  _1Bit_FullAdder _1bit_fulladder_4 (
    .A(Out_3), .B(_16bit_2_to_1_mux_2_out_3), .C_in(_1bit_fulladder_3_c_out), .S(_1bit_fulladder_4_s),
    .C_out(_1bit_fulladder_4_c_out));
  _1Bit_FullAdder _1bit_fulladder_5 (
    .A(Out_4), .B(_16bit_2_to_1_mux_2_out_4), .C_in(_1bit_fulladder_4_c_out), .S(_1bit_fulladder_5_s),
    .C_out(_1bit_fulladder_5_c_out));
  _1Bit_FullAdder _1bit_fulladder_6 (
    .A(Out_5), .B(_16bit_2_to_1_mux_2_out_5), .C_in(_1bit_fulladder_5_c_out), .S(_1bit_fulladder_6_s),
    .C_out(_1bit_fulladder_6_c_out));
  _1Bit_FullAdder _1bit_fulladder_7 (
    .A(Out_6), .B(_16bit_2_to_1_mux_2_out_6), .C_in(_1bit_fulladder_6_c_out), .S(_1bit_fulladder_7_s),
    .C_out(_1bit_fulladder_7_c_out));
  _1Bit_FullAdder _1bit_fulladder_8 (
    .A(Out_7), .B(_16bit_2_to_1_mux_2_out_7), .C_in(_1bit_fulladder_7_c_out), .S(_1bit_fulladder_8_s),
    .C_out(_1bit_fulladder_8_c_out));
  _1Bit_FullAdder _1bit_fulladder_9 (
    .A(Out_8), .B(_16bit_2_to_1_mux_2_out_8), .C_in(_1bit_fulladder_8_c_out), .S(_1bit_fulladder_9_s),
    .C_out(_1bit_fulladder_9_c_out));
  _1Bit_FullAdder _1bit_fulladder_10 (
    .A(Out_9), .B(_16bit_2_to_1_mux_2_out_9), .C_in(_1bit_fulladder_9_c_out), .S(_1bit_fulladder_10_s),
    .C_out(_1bit_fulladder_10_c_out));
  _1Bit_FullAdder _1bit_fulladder_11 (
    .A(Out_10), .B(_16bit_2_to_1_mux_2_out_10), .C_in(_1bit_fulladder_10_c_out), .S(_1bit_fulladder_11_s),
    .C_out(_1bit_fulladder_11_c_out));
  _1Bit_FullAdder _1bit_fulladder_12 (
    .A(Out_11), .B(_16bit_2_to_1_mux_2_out_11), .C_in(_1bit_fulladder_11_c_out), .S(_1bit_fulladder_12_s),
    .C_out(_1bit_fulladder_12_c_out));
  _1Bit_FullAdder _1bit_fulladder_13 (
    .A(Out_12), .B(_16bit_2_to_1_mux_2_out_12), .C_in(_1bit_fulladder_12_c_out), .S(_1bit_fulladder_13_s),
    .C_out(_1bit_fulladder_13_c_out));
  _1Bit_FullAdder _1bit_fulladder_14 (
    .A(Out_13), .B(_16bit_2_to_1_mux_2_out_13), .C_in(_1bit_fulladder_13_c_out), .S(_1bit_fulladder_14_s),
    .C_out(_1bit_fulladder_14_c_out));
  _1Bit_FullAdder _1bit_fulladder_15 (
    .A(Out_14), .B(_16bit_2_to_1_mux_2_out_14), .C_in(_1bit_fulladder_14_c_out), .S(_1bit_fulladder_15_s),
    .C_out(_1bit_fulladder_15_c_out));
  _1Bit_FullAdder _1bit_fulladder_16 (
    .A(Out_15), .B(_16bit_2_to_1_mux_2_out_15), .C_in(_1bit_fulladder_15_c_out), .S(_1bit_fulladder_16_s));  // open: C_out
endmodule
